# Fritzing sketch schematic (saved by Fritzing 0.9.2b)
breadboards: 1

parts:
  U1 = LCD-16X2 [package=lcd-16x2_noholes]
  Part1 = Arduino Pro Mini v13
  Q1 = Basic FET N-Channel [part_number="FER A SOUDER" package="DPak [SMD]"]
  U2 = LM358 [package=dip08]
  V1 = DC Power [voltage=5]
  U3 = POT [package=pot_alpha_rv16af-20]
  R1 = Resistor [tolerance=±5% resistance=220 package=THT]
  R2 = Resistor [tolerance=±5% resistance=220 part_number=THERMOCOUPLE package=THT]
  U5 = ENCODER_2LED [package=encoder_led_2]

nets:
  VSS: U1.VSS, U1.R_W, Part1.GND, Q1.source, U2.G$1_V-, V1.V-, U3.A, U5.B
  VDD: U1.VDD, Part1.VCC, U2.G$1_V+, V1.V+, U3.E, R1.Pin_1, U5.A
  N1: U1.VO, U3.S
  N2: U1.RS, Part1.D12/MISO
  N3: U1.E, Part1.D11_PWM/MOSI
  N4: U1.DB4, Part1.D5_PWM
  N5: U1.DB5, Part1.D4
  N6: U1.DB6, Part1.D3_PWM
  N7: U1.DB7, Part1.D2
  N8: Part1.A3, U5.+R
  N9: Part1.A2, U5.+G
  N10: Part1.A1, U5.SW
  N11: Part1.A0, U2.G$1_OUT
  N12: Part1.D6_PWM, Q1.Gate
  N13: Q1.drain, R1.Pin_0
  N14: U2.G$1_-IN, R2.Pin_1
  N15: U2.G$1_+IN, R2.Pin_0
